# Fritzing sketch Cheapspark (saved by Fritzing 0.9.2b)
circuit board: 6cm x 3cm
breadboards: 1

parts:
  R1 = Resistor [tolerance=±5% resistance=470 package=THT]
  R2 = Resistor [tolerance=±5% resistance=220 package=THT]
  3_3v = female pin header, 2 pins [form="♀ (female)"]
  5v = female pin header, 2 pins [form="♀ (female)"]
  S1 = Momentary Switch [package=ksa_sealed_tac_switch]
  S2 = Momentary Switch [package=ksa_sealed_tac_switch]
  B = mystery part, 15 pins [chip_label=?]
  A = mystery part, 15 pins [chip_label=?]
  S3 = Momentary Switch [package=ksa_sealed_tac_switch]
  Part1 = Arduino Nano (Rev3.0)
  5v_2 = mystery part, 3 pins [chip_label=?]
  GND = mystery part, 3 pins [chip_label=?]
  U1 = mystery part, 4 pins [chip_label=?]
  ESP = mystery part, 4 pins [chip_label=?]

nets:
  N1: R1.Pin_0, 5v.pin2, S1.2, S1.4, S2.2, S2.4, B.pin12, A.pin14, S3.2, S3.4, Part1.GND, GND.pin1, GND.pin2, GND.pin3, ESP.pin4
  N2: R1.Pin_1, R2.Pin_0, ESP.pin1
  N3: R2.Pin_1, B.pin15, Part1.D1/TX
  N4: 3_3v.pin1, U1.pin1, U1.pin3
  N5: 5v.pin1, A.pin12, Part1.5V, 5v_2.pin1, 5v_2.pin2, 5v_2.pin3
  N6: S1.3, A.pin6, Part1.A2
  N7: S2.3, A.pin5, Part1.A1
  N8: B.pin1, Part1.D12/MISO
  N9: B.pin2, Part1.D11/MOSI
  N10: B.pin3, Part1.D10
  N11: B.pin4, Part1.D9
  N12: B.pin5, Part1.D8
  N13: B.pin6, Part1.D7
  N14: B.pin7, Part1.D6
  N15: B.pin8, Part1.D5
  N16: B.pin9, Part1.D4
  N17: B.pin10, Part1.D3
  N18: B.pin11, Part1.D2
  N19: B.pin13, A.pin13, Part1.RESET
  N20: B.pin14, Part1.D0/RX, U1.pin4
  N21: A.pin1, Part1.D13/SCK
  N22: A.pin2, Part1.3V3
  N23: A.pin3, Part1.AREF
  N24: A.pin4, S3.3, Part1.A0
  N25: A.pin7, Part1.A3
  N26: A.pin8, Part1.A4
  N27: A.pin9, Part1.A5
  N28: A.pin10, Part1.A6
  N29: A.pin11, Part1.A7
  N30: A.pin15, Part1.VIN
